// Logisim project mlp_forward.circ as structural Verilog
module main (
  input  [7:0] wh1,
  input  EN,
  input  [7:0] b1,
  input  [7:0] w1,
  input  [7:0] bh,
  input  x1_b0__LSB,
  input  [7:0] w2,
  input  [7:0] w3,
  input  x2_b0,
  input  out_t,
  input  [7:0] w4,
  input  [7:0] wh2,
  input  [7:0] b2,
  output out_14
);

  wire CLK, drelu_1_out_2, subtractor_1_bout;
  wire [7:0] h1_out_2, h2_out_2, multiplexer_1_out, multiplexer_2_out, multiplexer_3_out, multiplexer_4_out,
       multiplexer_5_out, multiplexer_6_out, multiplexer_7_out, multiplexer_8_out, multiplexer_9_out,
       multiplier8_1_out_3, multiplier8_2_out_3, register_1_q, register_2_q, register_3_q, register_4_q,
       register_5_q, register_6_q, register_7_q, register_8_q, register_9_q, sig_yh_out_2, w1x1_out_3,
       w2x1_out_3, w3x2_out_3, w4x2_out_3, y1_out_4, y2_out_4, yh_out_4;

  Multiplexer #(.width(8), .enable("false")) multiplexer_1 (.in0(w1), .out(multiplexer_1_out), .sel(EN));  // open: in1
  Multiplexer #(.width(8), .enable("false")) multiplexer_2 (.in0(w2), .out(multiplexer_2_out), .sel(EN));  // open: in1
  Multiplexer #(.width(8), .enable("false")) multiplexer_3 (.in0(w4), .out(multiplexer_3_out), .sel(EN));  // open: in1
  Register register_1 (.D(multiplexer_1_out), .en(1'b1), .Q(register_1_q), .clk(CLK), .clr(1'b0));
  Register register_2 (.D(multiplexer_2_out), .en(1'b1), .Q(register_2_q), .clk(CLK), .clr(1'b0));
  Register register_3 (.D(multiplexer_4_out), .en(1'b1), .Q(register_3_q), .clk(CLK), .clr(1'b0));
  Multiplexer #(.width(8), .enable("false")) multiplexer_4 (.in0(w3), .out(multiplexer_4_out), .sel(EN));  // open: in1
  Register register_4 (.D(multiplexer_3_out), .en(1'b1), .Q(register_4_q), .clk(CLK), .clr(1'b0));
  Multiplexer #(.width(8), .enable("false")) multiplexer_5 (.in0(b1), .out(multiplexer_5_out), .sel(EN));  // open: in1
  multiplier1 w1x1 (.in_1(register_1_q), .in_2(x1_b0__LSB), .out_3(w1x1_out_3));
  multiplier1 w2x1 (.in_1(register_2_q), .in_2(x1_b0__LSB), .out_3(w2x1_out_3));
  Multiplexer #(.width(8), .enable("false")) multiplexer_6 (.in0(b2), .out(multiplexer_6_out), .sel(EN));  // open: in1
  Register register_5 (.D(multiplexer_5_out), .en(1'b1), .Q(register_5_q), .clk(CLK), .clr(1'b0));
  adder3 y1 (.in_1(register_5_q), .in_2(w1x1_out_3), .in_3(w3x2_out_3), .out_4(y1_out_4));
  multiplier1 w3x2 (.in_1(register_3_q), .in_2(x2_b0), .out_3(w3x2_out_3));
  multiplier1 w4x2 (.in_1(register_4_q), .in_2(x2_b0), .out_3(w4x2_out_3));
  Register register_6 (.D(multiplexer_6_out), .en(1'b1), .Q(register_6_q), .clk(CLK), .clr(1'b0));
  Multiplexer #(.width(8), .enable("false")) multiplexer_7 (.in0(wh1), .out(multiplexer_7_out), .sel(EN));  // open: in1
  // Probe on y1_out_4
  relu_mux h1 (.in_1(y1_out_4), .out_2(h1_out_2));
  adder3 y2 (.in_1(w2x1_out_3), .in_2(w4x2_out_3), .in_3(register_6_q), .out_4(y2_out_4));
  relu_mux h2 (.in_1(y2_out_4), .out_2(h2_out_2));
  // Probe on y2_out_4
  Register register_7 (.D(multiplexer_7_out), .en(1'b1), .Q(register_7_q), .clk(CLK), .clr(1'b0));
  // Probe on register_7_q
  drelu drelu_1 (.in_1(h1_out_2), .out_2(drelu_1_out_2));
  // Probe on h2_out_2
  multiplier8 multiplier8_1 (.in_1(register_7_q), .in_2(h1_out_2), .out_3(multiplier8_1_out_3));
  // Probe on multiplier8_1_out_3
  Multiplexer #(.width(8), .enable("false")) multiplexer_8 (.in0(wh2), .out(multiplexer_8_out), .sel(EN));  // open: in1
  Register register_8 (.D(multiplexer_8_out), .en(1'b1), .Q(register_8_q), .clk(CLK), .clr(1'b0));
  Multiplexer #(.width(8), .enable("false")) multiplexer_9 (.in0(bh), .out(multiplexer_9_out), .sel(EN));  // open: in1
  // Probe on multiplier8_2_out_3
  multiplier8 multiplier8_2 (.in_1(h2_out_2), .in_2(register_8_q), .out_3(multiplier8_2_out_3));
  Clock u_CLK (.out(CLK));
  Register register_9 (.D(multiplexer_9_out), .en(1'b1), .Q(register_9_q), .clk(CLK), .clr(1'b0));
  adder3 yh (.in_1(register_9_q), .in_2(multiplier8_1_out_3), .in_3(multiplier8_2_out_3), .out_4(yh_out_4));
  // Probe on yh_out_4
  sigmoid sig_yh (.in_1(yh_out_4), .out_2(sig_yh_out_2));
  round round (.in_1(sig_yh_out_2), .out_2(out_14));
  // Probe on sig_yh_out_2
  Subtractor subtractor_1 (.a(sig_yh_out_2), .b({3'b000, out_t, 4'b0000}), .bout(subtractor_1_bout));  // open: out, bin

  // Notes on the sheet:
  //   Standard 1 bit sign, 3 bit int, 4 bit decimals convention used, no bit shifting X XXX.XXXX
  //   adder3 last output 6bit.1bit
  //   out_c - out_t = de/dyh
endmodule

module multiplier1 (
  input  [7:0] in_1,
  input  in_2,
  output [7:0] out_3
);

  and and_1 (out_3[0], in_1[0], in_2);
  and and_2 (out_3[1], in_1[1], in_2);
  and and_3 (out_3[2], in_1[2], in_2);
  and and_4 (out_3[3], in_1[3], in_2);
  and and_5 (out_3[4], in_1[4], in_2);
  and and_6 (out_3[5], in_1[5], in_2);
  and and_7 (out_3[6], in_1[6], in_2);
  and and_8 (out_3[7], in_1[7], in_2);
endmodule

module pos_multiplier8 (
  input  [6:0] in_1,
  input  [6:0] in_2,
  output [7:0] out_3
);

  wire [7:0] adder_1_out, multiplier1_1_out_3, multiplier1_2_out_3, multiplier1_3_out_3, multiplier1_4_out_3,
       multiplier1_5_out_3, multiplier1_6_out_3, multiplier1_7_out_3;
  wire [8:0] adder_2_out;
  wire [8:8] adder_1_cout;
  wire [9:0] adder_3_out;
  wire [9:9] adder_2_cout;
  wire [10:0] adder_4_out;
  wire [10:10] adder_3_cout;
  wire [11:0] adder_5_out;
  wire [11:11] adder_4_cout;
  wire [12:0] adder_6_out;
  wire [12:12] adder_5_cout;
  wire [13:13] adder_6_cout;

  multiplier1 multiplier1_1 (.in_1({1'b0, in_1}), .in_2(in_2[0]), .out_3(multiplier1_1_out_3));
  multiplier1 multiplier1_2 (.in_1({1'b0, in_1}), .in_2(in_2[1]), .out_3(multiplier1_2_out_3));
  multiplier1 multiplier1_3 (.in_1({1'b0, in_1}), .in_2(in_2[2]), .out_3(multiplier1_3_out_3));
  multiplier1 multiplier1_4 (.in_1({1'b0, in_1}), .in_2(in_2[3]), .out_3(multiplier1_4_out_3));
  multiplier1 multiplier1_5 (.in_1({1'b0, in_1}), .in_2(in_2[4]), .out_3(multiplier1_5_out_3));
  multiplier1 multiplier1_6 (.in_1({1'b0, in_1}), .in_2(in_2[5]), .out_3(multiplier1_6_out_3));
  multiplier1 multiplier1_7 (.in_1({1'b0, in_1}), .in_2(in_2[6]), .out_3(multiplier1_7_out_3));
  // Probe on multiplier1_1_out_3
  // Probe on {adder_1_cout[8], adder_1_out}
  Adder adder_1 (
    .a(multiplier1_1_out_3), .b(multiplier1_2_out_3), .out(adder_1_out), .cout(adder_1_cout[8]));  // open: cin
  // Probe on {adder_2_cout[9], adder_2_out}
  Adder #(.width(9)) adder_2 (
    .a({adder_1_cout[8], adder_1_out}), .b({multiplier1_3_out_3[6:0], 2'b00}), .out(adder_2_out),
    .cout(adder_2_cout[9]));  // open: cin
  Adder #(.width(10)) adder_3 (
    .a({adder_2_cout[9], adder_2_out}), .b({multiplier1_4_out_3[6:0], 3'b000}), .out(adder_3_out),
    .cout(adder_3_cout[10]));  // open: cin
  Adder #(.width(11)) adder_4 (
    .a({adder_3_cout[10], adder_3_out}), .b({multiplier1_5_out_3[6:0], 4'b0000}), .out(adder_4_out),
    .cout(adder_4_cout[11]));  // open: cin
  // Probe on {adder_4_cout[11], adder_4_out}
  Adder #(.width(12)) adder_5 (
    .a({adder_4_cout[11], adder_4_out}), .b({multiplier1_6_out_3[6:0], {5{1'b0}}}), .out(adder_5_out),
    .cout(adder_5_cout[12]));  // open: cin
  // Probe on {adder_5_cout[12], adder_5_out}
  Adder #(.width(13)) adder_6 (
    .a({adder_5_cout[12], adder_5_out}), .b({multiplier1_7_out_3[6:0], {6{1'b0}}}),
    .out({adder_6_out[12:11], out_3[6:0], adder_6_out[3:0]}), .cout(adder_6_cout[13]));  // open: cin
  // Probe on {adder_6_cout[13], adder_6_out[12:11], out_3[6:0], adder_6_out[3:0]}
  // Probe on {adder_3_cout[10], adder_3_out}

  assign out_3[7] = 1'b0;

  // Notes on the sheet:
  //   this only handles pos-pos!
  //   8bit
  //   8bit
  //   9bit
  //   10bit
  //   11bit
  //   12bit
  //   13bit
  //   14bit
endmodule

module out (
  input  [7:0] in_1,
  output out_2
);

  wire not_1_out, or_1_out, or_2_out, or_3_out, or_4_out, or_5_out, or_6_out;

  or or_1 (or_1_out, in_1[0], in_1[1]);
  or or_2 (or_2_out, in_1[2], in_1[3]);
  or or_3 (or_3_out, in_1[4], in_1[5]);
  not not_1 (not_1_out, in_1[7]);
  or or_4 (or_4_out, or_1_out, or_2_out);
  or or_5 (or_5_out, or_3_out, in_1[6]);
  or or_6 (or_6_out, or_4_out, or_5_out);
  and and_1 (out_2, or_6_out, not_1_out);
endmodule

module adder3 (
  input  [7:0] in_1,
  input  [7:0] in_2,
  input  [7:0] in_3,
  output [7:0] out_4
);

  wire [7:0] adder2_1_out_3;

  adder2 adder2_1 (.in_1(in_1), .in_2(in_2), .out_3(adder2_1_out_3));
  adder2 adder2_2 (.in_1(adder2_1_out_3), .in_2(in_3), .out_3(out_4));
endmodule

module relu_mux (
  input  [7:0] in_1,
  output [7:0] out_2
);

  Multiplexer #(.width(8), .enable("false")) multiplexer_1 (.in0(in_1), .in1({8{1'b0}}), .out(out_2), .sel(in_1[7]));

  // Notes on the sheet:
  //   If first bit is 1, means neg number, will go to zero, else input remains as output
endmodule

module multiplier8 (
  input  [7:0] in_1,
  input  [7:0] in_2,
  output [7:0] out_3
);

  wire and_1_out, nor_1_out, xor_1_out;
  wire [6:0] multiplexer_3_out, multiplexer_4_out, multiplexer_5_out, multiplexer_6_out, multiplexer_7_out,
       multiplexer_8_out, negator_1_out, negator_2_out, negator_3_out;
  wire [7:0] multiplexer_1_out, multiplexer_2_out, negator_4_out, pos_multiplier8_1_out_3,
       pos_multiplier8_2_out_3, pos_multiplier8_3_out_3;

  and and_1 (and_1_out, in_1[7], in_2[7]);
  xor xor_1 (xor_1_out, in_1[7], in_2[7]);
  nor nor_1 (nor_1_out, in_1[7], in_2[7]);
  Multiplexer #(.width(8), .enable("false")) multiplexer_1 (
    .in0({8{1'b0}}), .in1(in_1), .out(multiplexer_1_out), .sel(xor_1_out));
  Multiplexer #(.width(8), .enable("false")) multiplexer_2 (
    .in0({8{1'b0}}), .in1(in_2), .out(multiplexer_2_out), .sel(xor_1_out));
  Multiplexer #(.width(7), .enable("false")) multiplexer_3 (
    .in0({7{1'b0}}), .in1(in_1[6:0]), .out(multiplexer_3_out), .sel(nor_1_out));
  Multiplexer #(.width(7), .enable("false")) multiplexer_4 (
    .in0({7{1'b0}}), .in1(in_1[6:0]), .out(multiplexer_4_out), .sel(and_1_out));
  Multiplexer #(.width(7), .enable("false")) multiplexer_5 (
    .in0({7{1'b0}}), .in1(in_2[6:0]), .out(multiplexer_5_out), .sel(and_1_out));
  // Probe on multiplexer_3_out
  // Probe on multiplexer_6_out
  Multiplexer #(.width(7), .enable("false")) multiplexer_6 (
    .in0({7{1'b0}}), .in1(in_2[6:0]), .out(multiplexer_6_out), .sel(nor_1_out));
  Negator #(.width(7)) negator_1 (.in(multiplexer_4_out), .out(negator_1_out));
  Negator #(.width(7)) negator_2 (.in(multiplexer_5_out), .out(negator_2_out));
  Multiplexer #(.width(7), .enable("false")) multiplexer_7 (
    .in0(multiplexer_1_out[6:0]), .in1(multiplexer_2_out[6:0]), .out(multiplexer_7_out),
    .sel(multiplexer_1_out[7]));
  Multiplexer #(.width(7), .enable("false")) multiplexer_8 (
    .in0(multiplexer_1_out[6:0]), .in1(multiplexer_2_out[6:0]), .out(multiplexer_8_out),
    .sel(multiplexer_2_out[7]));
  Negator #(.width(7)) negator_3 (.in(multiplexer_8_out), .out(negator_3_out));
  pos_multiplier8 pos_multiplier8_1 (
    .in_1(multiplexer_3_out), .in_2(multiplexer_6_out), .out_3(pos_multiplier8_1_out_3));
  pos_multiplier8 pos_multiplier8_2 (.in_1(negator_1_out), .in_2(negator_2_out), .out_3(pos_multiplier8_2_out_3));
  pos_multiplier8 pos_multiplier8_3 (.in_1(multiplexer_7_out), .in_2(negator_3_out), .out_3(pos_multiplier8_3_out_3));
  // Probe on pos_multiplier8_1_out_3
  Negator negator_4 (.in(pos_multiplier8_3_out_3), .out(negator_4_out));
  assign out_3 = pos_multiplier8_1_out_3 | pos_multiplier8_2_out_3 | negator_4_out;  // OR_Gate or_1, 8 bits wide

  // Notes on the sheet:
  //   positive
  //   negative
  //   pos*neg = neg (unless zero multiplication), negate positive multiplication output
endmodule

module drelu (
  input  [7:0] in_1,
  output out_2
);

  Multiplexer #(.enable("false")) multiplexer_1 (.in0(1'b1), .in1(1'b0), .out(out_2), .sel(in_1[7]));

  // Notes on the sheet:
  //   If first bit is 1, means neg number, will go to zero, else output =1
endmodule

module adder2 (
  input  [7:0] in_1,
  input  [7:0] in_2,
  output [7:0] out_3
);

  wire nor_1_out, xor_1_out;
  wire [6:0] adder_1_out, adder_2_out, multiplexer_3_out, multiplexer_4_out, multiplexer_5_out,
       multiplexer_6_out, multiplexer_7_out, multiplexer_8_out, negator_1_out, negator_2_out, negator_3_out,
       subtractor_1_out;
  wire [7:0] multiplexer_1_out, multiplexer_2_out, negator_4_out;
  wire [7:7] subtractor_1_bout;

  and and_1 (negator_4_out[7], in_1[7], in_2[7]);
  xor xor_1 (xor_1_out, in_1[7], in_2[7]);
  nor nor_1 (nor_1_out, in_1[7], in_2[7]);
  Multiplexer #(.width(8), .enable("false")) multiplexer_1 (
    .in0({8{1'b0}}), .in1(in_1), .out(multiplexer_1_out), .sel(xor_1_out));
  Multiplexer #(.width(8), .enable("false")) multiplexer_2 (
    .in0({8{1'b0}}), .in1(in_2), .out(multiplexer_2_out), .sel(xor_1_out));
  Multiplexer #(.width(7), .enable("false")) multiplexer_3 (
    .in0({7{1'b0}}), .in1(in_1[6:0]), .out(multiplexer_3_out), .sel(nor_1_out));
  Multiplexer #(.width(7), .enable("false")) multiplexer_4 (
    .in0({7{1'b0}}), .in1(in_1[6:0]), .out(multiplexer_4_out), .sel(negator_4_out[7]));
  Multiplexer #(.width(7), .enable("false")) multiplexer_5 (
    .in0({7{1'b0}}), .in1(in_2[6:0]), .out(multiplexer_5_out), .sel(negator_4_out[7]));
  Multiplexer #(.width(7), .enable("false")) multiplexer_6 (
    .in0({7{1'b0}}), .in1(in_2[6:0]), .out(multiplexer_6_out), .sel(nor_1_out));
  Negator #(.width(7)) negator_1 (.in(multiplexer_4_out), .out(negator_1_out));
  Negator #(.width(7)) negator_2 (.in(multiplexer_5_out), .out(negator_2_out));
  Multiplexer #(.width(7), .enable("false")) multiplexer_7 (
    .in0(multiplexer_1_out[6:0]), .in1(multiplexer_2_out[6:0]), .out(multiplexer_7_out),
    .sel(multiplexer_1_out[7]));
  Multiplexer #(.width(7), .enable("false")) multiplexer_8 (
    .in0(multiplexer_1_out[6:0]), .in1(multiplexer_2_out[6:0]), .out(multiplexer_8_out),
    .sel(multiplexer_2_out[7]));
  // Probe on multiplexer_7_out
  // Probe on multiplexer_8_out
  Adder #(.width(7)) adder_1 (.a(multiplexer_3_out), .b(multiplexer_6_out), .out(adder_1_out));  // open: cin, cout
  Adder #(.width(7)) adder_2 (.a(negator_1_out), .b(negator_2_out), .out(adder_2_out));  // open: cin, cout
  Negator #(.width(7)) negator_3 (.in(multiplexer_8_out), .out(negator_3_out));
  // Probe on {1'b0, adder_1_out}
  Negator #(.width(7)) negator_4 (.in(adder_2_out), .out(negator_4_out[6:0]));
  // Probe on negator_3_out
  // Probe on negator_4_out
  Subtractor #(.width(7)) subtractor_1 (
    .a(multiplexer_7_out), .b(negator_3_out), .out(subtractor_1_out), .bout(subtractor_1_bout[7]));  // open: bin
  // Probe on {subtractor_1_bout[7], subtractor_1_out}
  assign out_3 = {1'b0, adder_1_out} | negator_4_out | {subtractor_1_bout[7], subtractor_1_out};  // OR_Gate or_1, 8 bits wide

  // Notes on the sheet:
  //   positive
  //   negative
  //   positive
  //   negative
endmodule

module sigmoid (
  input  [7:0] in_1,
  output [7:0] out_2
);

  wire [1:0] multiplexer_2_out;
  wire [6:0] adder_1_out, multiplexer_1_out, negator_1_out;
  wire [7:0] exp_x_out_2;
  wire [8:0] bit_extender_1_out, divider_1_out, negator_2_out;

  exp_x exp_x (.in_1(in_1), .out_2(exp_x_out_2));
  // Probe on exp_x_out_2
  Adder adder_1 (.a(8'h10), .b(exp_x_out_2), .out({out_2[7], adder_1_out}));  // open: cin, cout
  // Probe on {out_2[7], adder_1_out}
  Negator #(.width(7)) negator_1 (.in(adder_1_out), .out(negator_1_out));
  Multiplexer #(.width(7), .disabled(0), .enable("false")) multiplexer_1 (
    .in0(adder_1_out), .in1(negator_1_out), .out(multiplexer_1_out), .sel(out_2[7]));
  assign bit_extender_1_out = {{2{1'b0}}, multiplexer_1_out};  // Bit_Extender bit_extender_1
  Divider #(.width(9)) divider_1 (.a(9'h100), .b(bit_extender_1_out), .out(divider_1_out));  // open: upper, rem
  // Probe on divider_1_out
  Negator #(.width(9)) negator_2 (.in(divider_1_out), .out(negator_2_out));
  Multiplexer #(.width(9), .disabled(0), .enable("false")) multiplexer_2 (
    .in0(divider_1_out), .in1(negator_2_out), .out({multiplexer_2_out, out_2[6:0]}), .sel(out_2[7]));

  // Notes on the sheet:
  //   shift the 1 to 4 bits to the left, pad 2 more binary
  //   remove 2 bit binary padding
endmodule

module exp_x (
  input  [7:0] in_1,
  output [7:0] out_2
);

  wire subtractor_1_bout;
  wire [6:0] adder_1_out, adder_2_out, adder_3_out, adder_4_out, demultiplexer_1_out0, demultiplexer_1_out1,
       MD_2_out_4, MD_3_out_4, MD_4_out_4, MD_out_4, multiplexer_1_out, negator_1_out, negator_2_out,
       subtractor_1_out, subtractor_2_out, subtractor_3_out;
  wire [7:7] subtractor_3_bout;

  Demultiplexer #(.width(7), .disabled(0), .enable("false")) demultiplexer_1 (
    .out0(demultiplexer_1_out0), .out1(demultiplexer_1_out1), .in(in_1[6:0]), .sel(in_1[7]));
  // Probe on demultiplexer_1_out0
  Negator #(.width(7)) negator_1 (.in(demultiplexer_1_out1), .out(negator_1_out));
  Adder #(.width(7)) adder_1 (.a(7'b0010000), .b(demultiplexer_1_out0), .out(adder_1_out));  // open: cin, cout
  multiply_divide MD (.in_1(demultiplexer_1_out0), .in_2(demultiplexer_1_out0), .in_3(7'b0000010), .out_4(MD_out_4));
  Subtractor #(.width(7)) subtractor_1 (
    .a(7'b0010000), .b(negator_1_out), .out(subtractor_1_out), .bout(subtractor_1_bout));  // open: bin
  // Probe on subtractor_1_out
  multiply_divide MD_2 (.in_1(negator_1_out), .in_2(negator_1_out), .in_3(7'b0000010), .out_4(MD_2_out_4));
  // Probe on negator_2_out
  Negator #(.width(7)) negator_2 (.in(subtractor_1_out), .out(negator_2_out));
  // Probe on MD_2_out_4
  multiply_divide MD_3 (.in_1(MD_2_out_4), .in_2(negator_1_out), .in_3(7'b0000011), .out_4(MD_3_out_4));
  // Probe on MD_out_4
  multiply_divide MD_4 (.in_1(MD_out_4), .in_2(demultiplexer_1_out0), .in_3(7'b0000011), .out_4(MD_4_out_4));
  Adder #(.width(7)) adder_2 (.a(adder_1_out), .b(MD_out_4), .out(adder_2_out));  // open: cin, cout
  Adder #(.width(7)) adder_3 (.a(subtractor_1_out), .b(MD_2_out_4), .out(adder_3_out));  // open: cin, cout
  Subtractor #(.width(7)) subtractor_2 (.a(MD_2_out_4), .b(negator_2_out), .out(subtractor_2_out));  // open: bin, bout
  Adder #(.width(7)) adder_4 (.a(adder_2_out), .b(MD_4_out_4), .out(adder_4_out));  // open: cin, cout
  Multiplexer #(.width(7), .disabled(0), .enable("false")) multiplexer_1 (
    .in0(adder_3_out), .in1(subtractor_2_out), .out(multiplexer_1_out), .sel(subtractor_1_bout));
  // Probe on MD_3_out_4
  Subtractor #(.width(7)) subtractor_3 (
    .a(multiplexer_1_out), .b(MD_3_out_4), .out(subtractor_3_out), .bout(subtractor_3_bout[7]));  // open: bin
  Multiplexer #(.width(8), .disabled(0), .enable("false")) multiplexer_2 (
    .in0({1'b0, adder_4_out}), .in1({subtractor_3_bout[7], subtractor_3_out}), .out(out_2), .sel(in_1[7]));

  // Notes on the sheet:
  //   x^2/2
  //   x^2/2
  //   x^3/6
  //   x^3/6
endmodule

module multiply_divide (
  input  [6:0] in_1,
  input  [6:0] in_2,
  input  [6:0] in_3,
  output [6:0] out_4
);

  wire [2:0] divider_1_out_2;
  wire [3:0] divider_1_out;
  wire [7:0] adder_1_out, multiplier1_1_out_3, multiplier1_2_out_3, multiplier1_3_out_3, multiplier1_4_out_3,
       multiplier1_5_out_3, multiplier1_6_out_3, multiplier1_7_out_3;
  wire [8:0] adder_2_out;
  wire [8:8] adder_1_cout;
  wire [9:0] adder_3_out;
  wire [9:9] adder_2_cout;
  wire [10:0] adder_4_out;
  wire [10:10] adder_3_cout;
  wire [11:0] adder_5_out;
  wire [11:11] adder_4_cout;
  wire [12:0] adder_6_out;
  wire [12:12] adder_5_cout;
  wire [13:0] bit_extender_1_out;
  wire [13:13] adder_6_cout;

  multiplier1 multiplier1_1 (.in_1({1'b0, in_1}), .in_2(in_2[0]), .out_3(multiplier1_1_out_3));
  multiplier1 multiplier1_2 (.in_1({1'b0, in_1}), .in_2(in_2[1]), .out_3(multiplier1_2_out_3));
  multiplier1 multiplier1_3 (.in_1({1'b0, in_1}), .in_2(in_2[2]), .out_3(multiplier1_3_out_3));
  multiplier1 multiplier1_4 (.in_1({1'b0, in_1}), .in_2(in_2[3]), .out_3(multiplier1_4_out_3));
  multiplier1 multiplier1_5 (.in_1({1'b0, in_1}), .in_2(in_2[4]), .out_3(multiplier1_5_out_3));
  multiplier1 multiplier1_6 (.in_1({1'b0, in_1}), .in_2(in_2[5]), .out_3(multiplier1_6_out_3));
  multiplier1 multiplier1_7 (.in_1({1'b0, in_1}), .in_2(in_2[6]), .out_3(multiplier1_7_out_3));
  // Probe on multiplier1_1_out_3
  // Probe on {adder_1_cout[8], adder_1_out}
  Adder adder_1 (
    .a(multiplier1_1_out_3), .b(multiplier1_2_out_3), .out(adder_1_out), .cout(adder_1_cout[8]));  // open: cin
  // Probe on {adder_2_cout[9], adder_2_out}
  Adder #(.width(9)) adder_2 (
    .a({adder_1_cout[8], adder_1_out}), .b({multiplier1_3_out_3[6:0], 2'b00}), .out(adder_2_out),
    .cout(adder_2_cout[9]));  // open: cin
  Adder #(.width(10)) adder_3 (
    .a({adder_2_cout[9], adder_2_out}), .b({multiplier1_4_out_3[6:0], 3'b000}), .out(adder_3_out),
    .cout(adder_3_cout[10]));  // open: cin
  Adder #(.width(11)) adder_4 (
    .a({adder_3_cout[10], adder_3_out}), .b({multiplier1_5_out_3[6:0], 4'b0000}), .out(adder_4_out),
    .cout(adder_4_cout[11]));  // open: cin
  // Probe on {adder_4_cout[11], adder_4_out}
  Adder #(.width(12)) adder_5 (
    .a({adder_4_cout[11], adder_4_out}), .b({multiplier1_6_out_3[6:0], {5{1'b0}}}), .out(adder_5_out),
    .cout(adder_5_cout[12]));  // open: cin
  // Probe on {adder_5_cout[12], adder_5_out}
  Adder #(.width(13)) adder_6 (
    .a({adder_5_cout[12], adder_5_out}), .b({multiplier1_7_out_3[6:0], {6{1'b0}}}), .out(adder_6_out),
    .cout(adder_6_cout[13]));  // open: cin
  assign bit_extender_1_out = {{7{1'b0}}, in_3};  // Bit_Extender bit_extender_1
  // Probe on {adder_6_cout[13], adder_6_out}
  // Probe on {adder_3_cout[10], adder_3_out}
  Divider #(.width(14)) divider_1 (
    .a({adder_6_cout[13], adder_6_out}), .b(bit_extender_1_out), .out({divider_1_out_2, out_4, divider_1_out}));  // open: upper, rem

  // Notes on the sheet:
  //   this only handles pos-pos!
  //   8bit
  //   8bit
  //   9bit
  //   10bit
  //   11bit
  //   12bit
  //   13bit
  //   14bit
endmodule

module round (
  input  [7:0] in_1,
  output out_2
);

  wire not_1_out, subtractor_1_bout;

  Subtractor #(.width(7)) subtractor_1 (.a(in_1[6:0]), .b(7'b0001000), .bout(subtractor_1_bout));  // open: out, bin
  not not_1 (not_1_out, subtractor_1_bout);
  Multiplexer #(.disabled(0), .enable("false")) multiplexer_1 (.in0(not_1_out), .in1(1'b0), .out(out_2), .sel(in_1[7]));

  // Notes on the sheet:
  //   round <0.5 to 0, >0.5 to 1
endmodule
